# Fritzing sketch BeatHeartSensor (saved by Fritzing 0.9.3b)

parts:
  U1 = ESP32S-HiLetgo [part_number=ESP32S-HiLetgo]
  SEN1 = Pulse Sensor [package=SIP-3]
  LED1 = LED - 5mm [color="Red (633nm)" package="5 mm [THT]"]

nets:
  N1: U1.3.3, LED1.anode
  N2: U1.GPIO34, SEN1.Signal
  GND: U1.GND, SEN1.GND, LED1.cathode
  VIN: U1.VIN, SEN1.VCC

custom parts:
  ESP32S-HiLetgo: HiLetgo ESP-WROOM-32 ESP32 ESP-32S Development Board 2.4GHz Dual-Mode WiFi + Bluetooth Dual Cores Microcontroller The ESP32 integrated with Antenna switches, RF Balun, power amplifiers, low-noise amplifiers, filters, and management modules, and the entire solution occupies the least area of PCB. 2.4 GHz Wi-Fi plus Bluetooth dual-mode chip, with TSMC Ultra-low power consumption 40nm technology,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
  Pulse Sensor: Pulse Sensor Optical Heart Beat Sensor
