# Fritzing sketch JoyStick (saved by Fritzing 0.9.3b)
breadboards: 1

parts:
  LED1 = LED - 5mm [color="Red (633nm)" package="5 mm [THT]"]
  LED2 = LED - 5mm [color="Red (633nm)" package="5 mm [THT]"]
  LED3 = LED - 5mm [color="Red (633nm)" package="5 mm [THT]"]
  LED4 = LED - 5mm [color="Red (633nm)" package="5 mm [THT]"]
  U1 = ESP32S-HiLetgo [part_number=ESP32S-HiLetgo]
  Componente1 = Thumb Joystick

nets:
  N1: LED1.cathode, LED2.cathode, LED3.cathode, LED4.cathode
  N2: LED1.anode, U1.GPIO25
  N3: LED2.anode, U1.GPIO33
  N4: LED3.anode, U1.GPIO26
  N5: LED4.anode, U1.GPIO27
  N6: U1.GPIO34, Componente1.HORZ
  N7: U1.GPIO35, Componente1.VERT
  GND: U1.GND, Componente1.GND
  VIN: U1.VIN, Componente1.VCC
  N8: U1.GPIO18, Componente1.SEL

custom parts:
  ESP32S-HiLetgo: HiLetgo ESP-WROOM-32 ESP32 ESP-32S Development Board 2.4GHz Dual-Mode WiFi + Bluetooth Dual Cores Microcontroller The ESP32 integrated with Antenna switches, RF Balun, power amplifiers, low-noise amplifiers, filters, and management modules, and the entire solution occupies the least area of PCB. 2.4 GHz Wi-Fi plus Bluetooth dual-mode chip, with TSMC Ultra-low power consumption 40nm technology,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
