# Fritzing sketch Matriz8x8Shock (saved by Fritzing 0.9.3b)

parts:
  Disp1 = LBT2088AH [part_number=LBT2088AH]
  U1 = MAX7219 [package=dil24]
  Součástka1 = Arduino Uno (Rev3)
  R1 = Resistor [tolerance=±5% resistance=20k package=THT]
  SW-1 = Vibration sensor module

nets:
  N1: Disp1.pin1, U1.SEGD
  N2: Disp1.pin2, U1.SEGF
  N3: Disp1.pin_3, U1.DIG1
  N4: Disp1.pin_4, U1.DIG2
  N5: Disp1.pin_5, U1.SEGG
  N6: Disp1.pin_6, U1.DIG4
  N7: Disp1.pin_7, U1.SEGE
  N8: Disp1.pin_8, U1.SEGB
  N9: Disp1.pin_9, U1.SEGDP
  N10: Disp1.pin_10, U1.DIG3
  N11: Disp1.pin_11, U1.DIG5
  N12: Disp1.pin_12, U1.SEGC
  N13: Disp1.pin_13, U1.DIG0
  N14: Disp1.pin_14, U1.SEGA
  N15: Disp1.pin_15, U1.DIG6
  N16: Disp1.pin_16, U1.DIG7
  N17: U1.DIN, Součástka1.D12/MISO
  GND: U1.GND, U1.GND2, Součástka1.GND, SW-1.Digital_output
  N18: U1.LOAD, Součástka1.D10_PWM/SS
  N19: U1.CLK, Součástka1.D11_PWM/MOSI
  N20: U1.ISET, R1.Pin_1
  VCC: U1.VCC, Součástka1.5V, R1.Pin_0
  N21: Součástka1.D2, SW-1.Ground
  3V3: Součástka1.3V3, SW-1.vcc

notes:
  Se utiliza una matriz de 8x32

custom parts:
  Vibration sensor module: Single-roller type full induction trigger switch. When no vibration or tilt, the product is ON conduction state, and in the steady state, when a vibration or tilt, the switch will be rendered instantly disconnect the conductive resistance increases, generating a current pulse signal, thereby triggering circuit. The default state of the swith is close Digital output Supply voltage:3.3V-5V On-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

// code stored in the sketch: disp8x8kode.ino

#include "MPU6050_6Axis_MotionApps20.h"
#if I2CDEV_IMPLEMENTATION == I2CDEV_ARDUINO_WIRE
    #include "Wire.h"
#endif
int UD;
int LR ;

#include "LedControl.h" //  importing the library
// DIN to 12, CLK to 11, CS to 10
LedControl lc=LedControl(12,11,10,1);
MPU6050 mpu;

// uncomment "OUTPUT_READABLE_QUATERNION" if you want to see the actual
// quaternion components in a [w, x, y, z] format (not best for parsing
// on a remote host such as Processing or something though)
//#define OUTPUT_READABLE_QUATERNION

// uncomment "OUTPUT_READABLE_EULER" if you want to see Euler angles
// (in degrees) calculated from the quaternions coming from the FIFO.
// Note that Euler angles suffer from gimbal lock (for more info, see
// http://en.wikipedia.org/wiki/Gimbal_lock)
//#define OUTPUT_READABLE_EULER

// uncomment "OUTPUT_READABLE_YAWPITCHROLL" if you want to see the yaw/
// pitch/roll angles (in degrees) calculated from the quaternions coming
// from the FIFO. Note this also requires gravity vector calculations.
// Also note that yaw/pitch/roll angles suffer from gimbal lock (for
// more info, see: http://en.wikipedia.org/wiki/Gimbal_lock)
//#define OUTPUT_READABLE_YAWPITCHROLL

// uncomment "OUTPUT_READABLE_REALACCEL" if you want to see acceleration
// components with gravity removed. This acceleration reference frame is
// not compensated for orientation, so +X is always +X according to the
// sensor, just without the effects of gravity. If you want acceleration
// compensated for orientation, us OUTPUT_READABLE_WORLDACCEL instead.
#define OUTPUT_READABLE_REALACCEL

// uncomment "OUTPUT_READABLE_WORLDACCEL" if you want to see acceleration
// components with gravity removed and adjusted for the world frame of
// reference (yaw is relative to initial orientation, since no magnetometer
// is present in this case). Could be quite handy in some cases.
//#define OUTPUT_READABLE_WORLDACCEL

// uncomment "OUTPUT_TEAPOT" if you want output that matches the
// format used for the InvenSense teapot demo
//#define OUTPUT_TEAPOT

#define INTERRUPT_PIN 2  // use pin 2 on Arduino Uno & most boards

bool blinkState = false;

bool dmpReady = false;  // set true if DMP init was successful
uint8_t mpuIntStatus;   // holds actual interrupt status byte from MPU
uint8_t devStatus;      // return status after each device operation (0 = success, !0 = error)
uint16_t packetSize;    // expected DMP packet size (default is 42 bytes)
uint16_t fifoCount;     // count of all bytes currently in FIFO
uint8_t fifoBuffer[64]; // FIFO storage buffer

Quaternion q;           // [w, x, y, z]         quaternion container
VectorInt16 aa;         // [x, y, z]            accel sensor measurements
VectorInt16 aaReal;     // [x, y, z]            gravity-free accel sensor measurements
VectorInt16 aaWorld;    // [x, y, z]            world-frame accel sensor measurements
VectorFloat gravity;    // [x, y, z]            gravity vector
float euler[3];         // [psi, theta, phi]    Euler angle container
float ypr[3];           // [yaw, pitch, roll]   yaw/pitch/roll container and gravity vector

uint8_t teapotPacket[14] = { '$', 0x02, 0,0, 0,0, 0,0, 0,0, 0x00, 0x00, '\r', '\n' };

// ===               INTERRUPT DETECTION ROUTINE                ===

volatile bool mpuInterrupt = false;     // indicates whether MPU interrupt pin has gone high
void dmpDataReady() {
    mpuInterrupt = true;
}

// ===                      INITIAL SETUP                       ===

void setup() {
    #if I2CDEV_IMPLEMENTATION == I2CDEV_ARDUINO_WIRE
        Wire.begin();
        Wire.setClock(400000); // 400kHz I2C clock. Comment this line if having compilation difficulties
    #elif I2CDEV_IMPLEMENTATION == I2CDEV_BUILTIN_FASTWIRE
        Fastwire::setup(400, true);
    #endif
    
    Serial.begin(38400);
    while (!Serial); // wait for Leonardo enumeration, others continue immediately
  lc.shutdown(0,false);// turn off power saving, enables display
  lc.setIntensity(0,15);// sets brightness (0~15 possible values)
  lc.clearDisplay(0);// clear screen
    Serial.println(F("Initializing I2C devices..."));
    mpu.initialize();
    pinMode(INTERRUPT_PIN, INPUT);
    Serial.println(F("Testing device connections..."));
    Serial.println(mpu.testConnection() ? F("MPU6050 connection successful") : F("MPU6050 connection failed"));
    Serial.println(F("Initializing DMP..."));
    devStatus = mpu.dmpInitialize();

    if (devStatus == 0) {
        Serial.println(F("Enabling DMP..."));
        mpu.setDMPEnabled(true);

        Serial.println(F("Enabling interrupt detection (Arduino external interrupt 0)..."));
        attachInterrupt(digitalPinToInterrupt(INTERRUPT_PIN), dmpDataReady, RISING);
        mpuIntStatus = mpu.getIntStatus();

        Serial.println(F("DMP ready! Waiting for first interrupt..."));
        dmpReady = true;

        packetSize = mpu.dmpGetFIFOPacketSize();
    } else {
       
        Serial.print(F("DMP Initialization failed (code "));
        Serial.print(devStatus);
        Serial.println(F(")"));
    }
}

// ===                    MAIN PROGRAM LOOP                     ===

void loop() {
    if (!dmpReady) return;

    while (!mpuInterrupt && fifoCount < packetSize) {
    
    }
    mpuInterrupt = false;
    mpuIntStatus = mpu.getIntStatus();

    fifoCount = mpu.getFIFOCount();

    if ((mpuIntStatus & 0x10) || fifoCount == 1024) {
        mpu.resetFIFO();

    } else if (mpuIntStatus & 0x02) {
        while (fifoCount < packetSize) fifoCount = mpu.getFIFOCount();
        mpu.getFIFOBytes(fifoBuffer, packetSize);    
        fifoCount -= packetSize;

        #ifdef OUTPUT_READABLE_QUATERNION
            // display quaternion values in easy matrix form: w x y z
            mpu.dmpGetQuaternion(&q, fifoBuffer);
            Serial.print("quat\t");
            Serial.print(q.w);
            Serial.print("\t");
            Serial.print(q.x);
            Serial.print("\t");
            Serial.print(q.y);
            Serial.print("\t");
            Serial.println(q.z);
        #endif

        #ifdef OUTPUT_READABLE_EULER
            // display Euler angles in degrees
            mpu.dmpGetQuaternion(&q, fifoBuffer);
            mpu.dmpGetEuler(euler, &q);
            Serial.print("euler\t");
            Serial.print(euler[0] * 180/M_PI);
            Serial.print("\t");
            Serial.print(euler[1] * 180/M_PI);
            Serial.print("\t");
            Serial.println(euler[2] * 180/M_PI);
        #endif

        #ifdef OUTPUT_READABLE_YAWPITCHROLL
            // display Euler angles in degrees
            mpu.dmpGetQuaternion(&q, fifoBuffer);
            mpu.dmpGetGravity(&gravity, &q);
            mpu.dmpGetYawPitchRoll(ypr, &q, &gravity);
            Serial.print("ypr\t");
            Serial.print(ypr[0] * 180/M_PI);
            Serial.print("\t");
            Serial.print(ypr[1] * 180/M_PI);
            Serial.print("\t");
            Serial.println(ypr[2] * 180/M_PI);
        #endif

        #ifdef OUTPUT_READABLE_REALACCEL
            // display real acceleration, adjusted to remove gravity
            mpu.dmpGetQuaternion(&q, fifoBuffer);
            mpu.dmpGetAccel(&aa, fifoBuffer);
            mpu.dmpGetGravity(&gravity, &q);
            mpu.dmpGetLinearAccel(&aaReal, &aa, &gravity);
            Serial.print("areal\t");
            Serial.print(aaReal.x);
            Serial.print("\t");
            Serial.print(aaReal.y);
            Serial.print("\t");
            Serial.println(aaReal.z);
        #endif

        #ifdef OUTPUT_READABLE_WORLDACCEL
            // display initial world-frame acceleration, adjusted to remove gravity
            // and rotated based on known orientation from quaternion
            mpu.dmpGetQuaternion(&q, fifoBuffer);
            mpu.dmpGetAccel(&aa, fifoBuffer);
            mpu.dmpGetGravity(&gravity, &q);
            mpu.dmpGetLinearAccel(&aaReal, &aa, &gravity);
            mpu.dmpGetLinearAccelInWorld(&aaWorld, &aaReal, &q);
            Serial.print("aworld\t");
            Serial.print(aaWorld.x);
            Serial.print("\t");
            Serial.print(aaWorld.y);
            Serial.print("\t");
            Serial.println(aaWorld.z);
        #endif
    
        #ifdef OUTPUT_TEAPOT
            // display quaternion values in InvenSense Teapot demo format:
            teapotPacket[2] = fifoBuffer[0];
            teapotPacket[3] = fifoBuffer[1];
            teapotPacket[4] = fifoBuffer[4];
            teapotPacket[5] = fifoBuffer[5];
            teapotPacket[6] = fifoBuffer[8];
            teapotPacket[7] = fifoBuffer[9];
            teapotPacket[8] = fifoBuffer[12];
            teapotPacket[9] = fifoBuffer[13];
            Serial.write(teapotPacket, 14);
            teapotPacket[11]++; // packetCount, loops at 0xFF on purpose
        #endif
  UD = aaReal.x; // read analog value at pin A1 and stores as UD
  LR = aaReal.y;  // read analog value at pin A0 and stores as LR

  char x_translate = map(LR, -4000, 4000, 0, 7); 
  char y_translate = map(UD, -4000, 4000, 7, 0);

    lc.clearDisplay(0);
    lc.setLed(0,x_translate,y_translate,true);  

    }
     delay(0);
    }
