# Fritzing sketch MotorTouch (saved by Fritzing 0.9.3b)
breadboards: 1

parts:
  U1 = ESP32S-HiLetgo [part_number=ESP32S-HiLetgo]
  S1 = H-Bridge with L298N
  M1 = DC Motor
  part = TTP223B Capacitive Touch Sensor Module

nets:
  N1: U1.3.3, part.VCC
  GND: U1.GND, S1.GND, part.GND
  VIN: U1.VIN, S1.5V
  N2: U1.GPIO4, S1.IN1
  N3: U1.GPIO5, S1.IN2
  N4: U1.GPIO21, part.SIG
  N5: S1.M1-01, M1.pin_1
  N6: S1.M1-02, M1.pin_2

custom parts:
  ESP32S-HiLetgo: HiLetgo ESP-WROOM-32 ESP32 ESP-32S Development Board 2.4GHz Dual-Mode WiFi + Bluetooth Dual Cores Microcontroller The ESP32 integrated with Antenna switches, RF Balun, power amplifiers, low-noise amplifiers, filters, and management modules, and the entire solution occupies the least area of PCB. 2.4 GHz Wi-Fi plus Bluetooth dual-mode chip, with TSMC Ultra-low power consumption 40nm technology,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
  H-Bridge with L298N: h-bridge
  TTP223B Capacitive Touch Sensor Module: The TTP223B capacitive touch sensor module uses the TTP223B IC. The appropriate voltage is approximately 2 to 5.5 volts.
