# Fritzing sketch TempAndHumidity (saved by Fritzing 0.9.3b)

parts:
  DHT1 = DHT11 Humitidy and Temperature Sensor
  U1 = ESP32S-HiLetgo [part_number=ESP32S-HiLetgo]

nets:
  VDD: DHT1.VDD, U1.VIN
  N1: DHT1.DATA, U1.GPIO10
  GND: DHT1.GND, U1.GND

custom parts:
  DHT11 Humitidy and Temperature Sensor: DHT11 Humidity and Temperature Sensor
  ESP32S-HiLetgo: HiLetgo ESP-WROOM-32 ESP32 ESP-32S Development Board 2.4GHz Dual-Mode WiFi + Bluetooth Dual Cores Microcontroller The ESP32 integrated with Antenna switches, RF Balun, power amplifiers, low-noise amplifiers, filters, and management modules, and the entire solution occupies the least area of PCB. 2.4 GHz Wi-Fi plus Bluetooth dual-mode chip, with TSMC Ultra-low power consumption 40nm technology,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
